# Fritzing sketch AnimStationWiring (saved by Fritzing 1.0.1rc)
breadboards: 1

parts:
  Mod1 = Raspberry Pi 4B
  LED1 = smd LED [color="White (6500K)" package="1206 [SMD]"]
  LED2 = smd LED [color="Red (633nm)" package="1206 [SMD]"]
  LED3 = smd LED [color="Green (555nm)" package="1206 [SMD]"]
  S4 = Taiway 100-SP-X-T1 SPDT Miniature Toggle Switch [part_number=100-SP-X-T1-0-0-B1-M2 package=THT]
  S5 = Taiway 100-SP-X-T1 SPDT Miniature Toggle Switch [part_number=100-SP-X-T1-0-0-B1-M2 package=THT]
  S6 = Taiway 100-SP-X-T1 SPDT Miniature Toggle Switch [part_number=100-SP-X-T1-0-0-B1-M2 package=THT]

nets:
  3.3V: Mod1.3V3, LED1.anode, LED2.anode, LED3.anode, S4.L2, S5.L2, S6.L2
  N1: Mod1.GPIO24, S6.COM
  N2: Mod1.GPIO25, S5.COM
  GND: Mod1.GND, LED1.cathode, LED2.cathode, LED3.cathode, S4.L1, S5.L1, S6.L1
  N3: Mod1.GPIO12, S4.COM

notes:
  Each switch/LED set represents 1 arcade button/LED combo. Common pin on switches are connected to Pi GPIO pins.
  Normally open (NO) connected to GND
  Normally closed (NC) connected to 3.3V
